# Fritzing sketch CLASIFICADOR DE FRUTAS (saved by Fritzing 0.9.5d)
breadboards: 1

parts:
  SparkFun_ESP32_Thing1 = SparkFun ESP32 Thing [part_number=DEV-13907]
  M1 = Stepper Motor - Bipolar
  S1 = Pushbutton [package="[THT]"]
  S2 = Pushbutton [package="[THT]"]
  R4 = Resistor [tolerance=±5% resistance=10k package=THT]  # not connected
  Pololu_A2 = DRV 8825 Stepper Motor Carrier, High Current [part_number="DRV 8825"]
  Power_plug1 = Power plug
  R5 = Resistor [tolerance=±5% resistance=10k package=THT]
  LED1 = LED - 5mm [color="Yellow (592nm)" package="5 mm [THT]"]
  LED3 = LED - 5mm [color="Blue (430nm)" package="5 mm [THT]"]
  LED4 = LED - 5mm [color="Green (570nm)" package="5 mm [THT]"]
  LED2 = LED - 5mm [color="Red (635nm)" package="5 mm [THT]"]
  R6 = Resistor [tolerance=±5% resistance=220 package=THT]
  R7 = Resistor [tolerance=±5% resistance=220 package=THT]
  R9 = Resistor [tolerance=±5% resistance=220 package=THT]
  R8 = Resistor [tolerance=±5% resistance=220 package=THT]

nets:
  N1: SparkFun_ESP32_Thing1.27, R9.Pin_1
  N2: SparkFun_ESP32_Thing1.GND, LED1.cathode, LED3.cathode, LED4.cathode, LED2.cathode
  N3: M1.A, Pololu_A2.OUT_2B
  N4: M1.C, Pololu_A2.OUT_2A
  N5: M1.B, Pololu_A2.OUT_1A
  N6: M1.D, Pololu_A2.OUT_1B
  N7: S1.Pin_1, S1.Pin_2
  N8: S1.Pin_3, S1.Pin_4, S2.Pin_3, S2.Pin_4
  N9: S2.Pin_1, S2.Pin_2, R5.Pin_0
  N10: Pololu_A2.VOLTAGE_ST/_MT, Power_plug1.VCC
  N11: Pololu_A2.GROUND_ST/_MT, Power_plug1.GND, R5.Pin_1
  N12: LED1.anode, R6.Pin_0
  N13: LED3.anode, R7.Pin_0
  N14: LED4.anode, R9.Pin_0
  N15: LED2.anode, R8.Pin_0

custom parts:
  SparkFun ESP32 Thing: The SparkFun ESP32 Thing is a comprehensive development platform for Espressif’s ESP32, their super-charged version of the popular ESP8266. Like the 8266, the ESP32 is a WiFi-compatible microcontroller, but to that it adds support for Bluetooth low-energy (i.e BLE, BT4.0, Bluetooth Smart), and nearly 30 I/O pins. The ESP32’s power and versatility will make it the foundation of IoT and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
